# Fritzing sketch schemat_polaczen (saved by Fritzing 0.9.3b)

parts:
  LCM1602_IIC1 = LCM1602 IIC [part_number="LCM1602 IIC" chip_label="LCM1602 IIC" package="DIP (Dual Inline) [THT]"]
  LCD1 = LCD screen
  PCB2 = RTC_DS1302_module
  Part1 = Arduino Uno (Rev3) - ICSP
  S1 = Square Pushbutton
  S2 = Square Pushbutton

nets:
  VSS: LCM1602_IIC1.VSS, LCD1.VSS
  VDD: LCM1602_IIC1.VDD, LCD1.VDD
  N1: LCM1602_IIC1.V0, LCD1.V0
  N2: LCM1602_IIC1.RS, LCD1.RS
  N3: LCM1602_IIC1.RW, LCD1.R/W
  N4: LCM1602_IIC1.E, LCD1.E
  N5: LCM1602_IIC1.D0, LCD1.DB0
  N6: LCM1602_IIC1.D1, LCD1.DB1
  N7: LCM1602_IIC1.D2, LCD1.DB2
  N8: LCM1602_IIC1.D3, LCD1.DB3
  N9: LCM1602_IIC1.D4, LCD1.DB4
  N10: LCM1602_IIC1.D5, LCD1.DB5
  N11: LCM1602_IIC1.D6, LCD1.DB6
  N12: LCM1602_IIC1.D7, LCD1.DB7
  N13: LCM1602_IIC1.A, LCD1.LED+
  N14: LCM1602_IIC1.K, LCD1.LED-
  GND: LCM1602_IIC1.GND, PCB2.GND, Part1.GND, S1.leg0, S2.leg0
  VCC: LCM1602_IIC1.VCC, PCB2.VCC, Part1.5V
  N15: LCM1602_IIC1.SDA, PCB2.DAT, Part1.A4/SDA
  N16: LCM1602_IIC1.SCL, PCB2.CLK, Part1.A5/SCL
  N17: Part1.D8, S2.leg1
  N18: Part1.D7, S1.leg1

custom parts:
  LCM1602 IIC: I2C-Module to use a 1602 or 2004 LCD on with the wire.h libory Serial LCD Modul
  RTC_DS1302_module: Arduino module DS1302 SPI Real Time Clock
